// Logisim project Controller.circ as structural Verilog: 1 circuit, main circuit Controller
module Controller (
  input  [15:0] Inst,
  input  [3:0] FlagsIn,
  input  Clk,
  input  Reset,
  output Carry,
  output DP_Shift,
  output Imm32_Enable,
  output [4:0] Imm5,
  output [31:0] Imm32,
  output [3:0] ALU_Opcode,
  output [2:0] Rm,
  output [2:0] Rn,
  output [2:0] Rd,
  output [3:0] Flags,
  output [31:0] RAM_Addr,
  output Load,
  output Store,
  output [31:0] SP,
  output [15:0] PC
);

  wire conditional_1_verified, load_store_1_pc_hold, not_1_out, opcode_decoder_1_p2, opcode_decoder_1_p3,
       opcode_decoder_1_p4, opcode_decoder_1_p5, opcode_decoder_1_p6, shift_add_sub_mov_1_carry,
       sp_address_1_write_enable;
  wire [2:0] data_processing_1_rd, data_processing_1_rm, data_processing_1_rn, load_store_1_rd,
       load_store_1_rm, or_3_out, shift_add_sub_mov_1_rd, shift_add_sub_mov_1_rm, shift_add_sub_mov_1_rn;
  wire [3:0] data_processing_1_alu_opcode, data_processing_1_flags_update_mask, or_1_out,
       shift_add_sub_mov_1_alu_opcode, shift_add_sub_mov_1_flags_update_mask;
  wire [10:0] conditional_1_offset;
  wire [15:0] adder_1_out, adder_2_out, bit_extender_1_out;
  wire [31:0] sp_address_1_new_stack_pointer;

  Register #(.width(32)) Stack_Pointer (
    .D(sp_address_1_new_stack_pointer), .en(sp_address_1_write_enable), .clk(Clk), .Q(SP), .clr(Reset));
  // Opcode_Decoder opcode_decoder_1: pin names not known; wires that end beside it: Inst[15:10], opcode_decoder_1_p2, opcode_decoder_1_p3, opcode_decoder_1_p4, opcode_decoder_1_p5, opcode_decoder_1_p6
  assign or_1_out = data_processing_1_flags_update_mask | shift_add_sub_mov_1_flags_update_mask;  // OR_Gate or_1, 4 bits wide
  Shift_Add_Sub_Mov shift_add_sub_mov_1 (
    .Flags_Update_Mask(shift_add_sub_mov_1_flags_update_mask), .Carry(shift_add_sub_mov_1_carry),
    .Imm32_Enable(Imm32_Enable), .Rm(shift_add_sub_mov_1_rm), .Rn(shift_add_sub_mov_1_rn),
    .Rd(shift_add_sub_mov_1_rd), .Imm5(Imm5), .Imm32(Imm32), .ALU_Opcode(shift_add_sub_mov_1_alu_opcode),
    .Instruction(Inst), .Enable(opcode_decoder_1_p2));
  Data_Processing data_processing_1 (
    .Rn(data_processing_1_rn), .Rm(data_processing_1_rm), .ALU_Opcode(data_processing_1_alu_opcode),
    .Flags_Update_Mask(data_processing_1_flags_update_mask), .Rd(data_processing_1_rd), .Instruction(Inst),
    .Enable(opcode_decoder_1_p3));
  Flags_APSR flags_apsr_1 (.Update_Mask(or_1_out), .Flags_In(FlagsIn), .Clk(Clk), .Rst(Reset), .Flags_Out(Flags));
  Load_Store load_store_1 (
    .Load(Load), .PC_Hold(load_store_1_pc_hold), .Rm(load_store_1_rm), .Rd(load_store_1_rd),
    .RAM_Addr(RAM_Addr), .Store(Store), .Stack_Pointer(SP), .Instruction(Inst), .Clk(Clk), .Reset(Reset),
    .Enable(opcode_decoder_1_p4));
  assign bit_extender_1_out = {{5{conditional_1_offset[10]}}, conditional_1_offset};  // Bit_Extender bit_extender_1
  Conditional conditional_1 (
    .Offset(conditional_1_offset), .Verified(conditional_1_verified), .Instruction(Inst), .Z(Flags[2]),
    .C(Flags[1]), .N(Flags[3]), .V(Flags[0]), .Enable(opcode_decoder_1_p6));
  SP_Address sp_address_1 (
    .New_Stack_Pointer(sp_address_1_new_stack_pointer), .Write_Enable(sp_address_1_write_enable),
    .Stack_Pointer(SP), .Instruction(Inst), .Enable(opcode_decoder_1_p5));
  Adder #(.width(16)) adder_1 (.a(16'h3), .b(bit_extender_1_out), .out(adder_1_out), .cin(1'b0));  // open: cout
  Adder #(.width(16)) adder_2 (.a(adder_1_out), .b(PC), .out(adder_2_out), .cin(1'b0));  // open: cout
  and and_1 (DP_Shift, opcode_decoder_1_p2, ~opcode_decoder_1_p3);  // AND_Gate
  not not_1 (not_1_out, load_store_1_pc_hold);
  Counter #(.max('hffff), .trigger("falling"), .width(16)) counter_1 (
    .clr(Reset), .load(conditional_1_verified), .up(1'b1), .count(not_1_out), .clk(Clk), .D(adder_2_out),
    .Q(PC));  // open: carry
  Multiplexer #(.enable("false")) multiplexer_1 (
    .in0(Flags[1]), .in1(shift_add_sub_mov_1_carry), .out(Carry), .sel(DP_Shift));
  assign Rm = shift_add_sub_mov_1_rm | data_processing_1_rm | load_store_1_rm;  // OR_Gate or_2, 3 bits wide
  assign or_3_out = shift_add_sub_mov_1_rn | data_processing_1_rn;  // OR_Gate or_3, 3 bits wide
  assign ALU_Opcode = shift_add_sub_mov_1_alu_opcode | data_processing_1_alu_opcode;  // OR_Gate or_4, 4 bits wide
  Multiplexer #(.enable("false"), .width(3)) multiplexer_2 (
    .in0(or_3_out), .in1(Rm), .out(Rn), .sel(opcode_decoder_1_p4));
  assign Rd = shift_add_sub_mov_1_rd | data_processing_1_rd | load_store_1_rd;  // OR_Gate or_5, 3 bits wide

  // Notes on the sheet:
  //   Extract carry
  //   Extract Opcode
  //   IF Reg_Imm=1 THEN use shift value from register ELSE use shift value from Imm5
  //   Buffer flags for next instruction
  //   Add 3 to offset because ARM pre-increments PC
  //   and does an additional prefetch operation
endmodule
