// Logisim project Machine.circ as structural Verilog: 2 circuits, main circuit main
module main (
);

  wire Clk_Button_out, Rst_Button_out;
  wire [7:0] RAM_Addr, ROM_Addr;
  wire [15:0] ROM_1_data_2;
  wire [31:0] CPU_1_r0, CPU_1_r1, CPU_1_r2, CPU_1_r3, CPU_1_r4, CPU_1_r5, CPU_1_r6, CPU_1_r7, rom_1_data;

  // Probe on RAM_Addr
  ROM #(.dataWidth(32)) rom_1 (.addr(RAM_Addr), .data(rom_1_data));
  Button Clk_Button (.out(Clk_Button_out));
  Button Rst_Button (.out(Rst_Button_out));
  // Probe on ROM_Addr
  ROM #(.dataWidth(16)) ROM_1_dup2 (.addr(ROM_Addr), .data(ROM_1_data_2));
  // Probe on CPU_1_r3
  // Probe on CPU_1_r2
  // Probe on CPU_1_r1
  // Probe on CPU_1_r0
  // Probe on CPU_1_r7
  // Probe on CPU_1_r6
  // Probe on CPU_1_r5
  // Probe on CPU_1_r4
  CPU CPU_1 (
    .Clk(Clk_Button_out), .ROM_Addr(ROM_Addr), .Rst(Rst_Button_out), .ROM_In(ROM_1_data_2),
    .RAM_Addr(RAM_Addr), .RAM_In(rom_1_data), .R0(CPU_1_r0), .R1(CPU_1_r1), .R2(CPU_1_r2), .R3(CPU_1_r3),
    .R4(CPU_1_r4), .R5(CPU_1_r5), .R6(CPU_1_r6), .R7(CPU_1_r7));  // open: RAM_Out

  // Notes on the sheet:
  //   contents of rom_1 (hex, n*v repeats v):
  //   1 3 2 4
  //   contents of ROM_1 (hex, n*v repeats v):
  //   9800 9900 1a08 d005 9a02 9801 c9 4308
endmodule

module CPU (
  input  [31:0] RAM_In,
  input  [15:0] ROM_In,
  input  Clk,
  input  Rst,
  output [7:0] ROM_Addr,
  output [7:0] RAM_Addr,
  output [31:0] RAM_Out,
  output [31:0] R3,
  output [31:0] R7,
  output [31:0] R2,
  output [31:0] R6,
  output [31:0] R1,
  output [31:0] R5,
  output [31:0] R0,
  output [31:0] R4
);

  wire Controller_1_p4, Controller_1_p6, Controller_1_p7, Controller_1_p8, Controller_1_p9, Controller_1_p10,
       Controller_1_p11, Controller_1_p14, Controller_1_p15, Regs_1_p15;
  wire [4:0] Controller_1_p13, multiplexer_3_out;
  wire [31:0] ALU_1_p5, bit_extender_1_out, multiplexer_1_out, multiplexer_2_out;

  // Controller Controller_1: pin names not known; wires that end beside it: ROM_In, Clk, Rst, Controller_1_p4, ROM_Addr, Controller_1_p6, Controller_1_p7, Controller_1_p8, Controller_1_p9, Controller_1_p10, Controller_1_p11, RAM_Addr, Controller_1_p13, Controller_1_p14, Controller_1_p15
  Multiplexer #(.width(32), .enable("false")) multiplexer_1 (
    .in0(ALU_1_p5), .in1(RAM_In), .out(multiplexer_1_out), .sel(Controller_1_p6));
  assign bit_extender_1_out = {{24{RAM_Addr[7]}}, RAM_Addr};  // Bit_Extender bit_extender_1
  Multiplexer #(.width(32), .enable("false")) multiplexer_2 (
    .in0(bit_extender_1_out), .in1(multiplexer_1_out), .out(multiplexer_2_out), .sel(Controller_1_p7));
  // BancRegistre Regs_1: pin names not known; wires that end beside it: multiplexer_2_out, Controller_1_p9, Clk, R0, Rst, R1, R2, R3, R4, Controller_1_p10, R5, R6, Controller_1_p11, R7, Regs_1_p15, RAM_Out
  Multiplexer #(.width(5), .enable("false")) multiplexer_3 (
    .in0(RAM_Out[4:0]), .in1(Controller_1_p13), .out(multiplexer_3_out), .sel(Controller_1_p14));
  // ALU ALU_1: pin names not known; wires that end beside it: multiplexer_3_out, RAM_Out, Controller_1_p8, Controller_1_p15, ALU_1_p5, Regs_1_p15, Controller_1_p4

  // Notes on the sheet:
  //   RAM/ALU Input selector
  //   Use data from register or immediate for shift
  //   Imm8 input for Move
endmodule
